// Logisim project GnebehiEtPerrot.circ as structural Verilog: 5 circuits, main circuit main
module main (
  input  _1___parcours_en_avant,
  input  _1___parcour_du_sequenceur_au_premier,
  input  [7:0] A,
  input  [7:0] B,
  input  [1:0] \Opérande ,
  input  Activation___1
);

  wire horloge_out, sequenceur_1_retenue, \sequenceur_1_si_1_alors_debordement___mauvais_résultat ,
       \unité_de_calcul_1_retenue ;
  wire [2:0] counter_1_q;
  wire [7:0] \sequenceur_1_résultat , \unité_de_calcul_1_résultat_8_bits ;
  wire [14:0] rom_1_data;

  Clock #(.highDuration(5), .lowDuration(5)) horloge (.out(horloge_out));
  // Probe on A
  // Probe on B
  Counter #(.width(3), .max('h7)) counter_1 (
    .load(1'b0), .D(3'b000), .count(_1___parcours_en_avant), .Q(counter_1_q), .clk(horloge_out),
    .clr(_1___parcour_du_sequenceur_au_premier));  // open: carry
  \Unité_de_Calcul  \unité_de_calcul_1  (
    .\entré_8_bits_A (A), .\entré_8_bits_B (B), .\Opérande (\Opérande ), .Activation___1(Activation___1),
    .Retenue(\unité_de_calcul_1_retenue ),
    .\_1___debordement_de_la_somme_alors_le_résultat_est_faux (\unité_de_calcul_1_retenue ),
    .\Résultat_8_bits (\unité_de_calcul_1_résultat_8_bits ));  // open: out_8
  LED led_1 (.in(\unité_de_calcul_1_retenue ));
  Sequenceur sequenceur_1 (
    .INSTRUCTIONS(rom_1_data),
    .\Si_1_Alors_debordement___mauvais_résultat (\sequenceur_1_si_1_alors_debordement___mauvais_résultat ),
    .Retenue(sequenceur_1_retenue), .\résultat (\sequenceur_1_résultat ));
  ROM #(.addrWidth(3), .dataWidth(15)) rom_1 (.addr(counter_1_q), .data(rom_1_data), .sel(1'b1));
  // Probe on \unité_de_calcul_1_résultat_8_bits 
  // Probe on \sequenceur_1_résultat 
  LED led_2 (.in(\sequenceur_1_si_1_alors_debordement___mauvais_résultat ));
  // Probe on sequenceur_1_retenue

  // Notes on the sheet:
  //   1 = parcours en arrière depuis le point de départ
  //   @dresse de point de départ
  //   0 = desactiver la meoire ROM
  //   contents of rom_1 (hex, n*v repeats v):
  //   503 c01 1104 202 16
endmodule

module \Banc_de_Régistre  (
  input  [7:0] \Entré ,
  input  Ecrire_1_ou_Lire_0,
  input  [1:0] adresse,
  input  Activation,
  output [7:0] out_5
);

  wire demultiplexer_1_out0, demultiplexer_1_out1, demultiplexer_1_out2, demultiplexer_1_out3, horloge_out,
       not_1_out;
  wire [7:0] demultiplexer_2_out0, demultiplexer_2_out1, demultiplexer_2_out2, demultiplexer_2_out3,
       multiplexer_1_out, register_1_q, register_2_q, register_3_q, register_4_q;

  // Probe on adresse
  Clock horloge (.out(horloge_out));
  Demultiplexer #(.select(2)) demultiplexer_1 (
    .out0(demultiplexer_1_out0), .out1(demultiplexer_1_out1), .out2(demultiplexer_1_out2),
    .out3(demultiplexer_1_out3), .in(horloge_out), .sel(adresse), .en(Activation));
  Demultiplexer #(.select(2), .width(8)) demultiplexer_2 (
    .out0(demultiplexer_2_out0), .out1(demultiplexer_2_out1), .out2(demultiplexer_2_out2),
    .out3(demultiplexer_2_out3), .in(\Entré ), .sel(adresse), .en(horloge_out));
  Register register_1 (.D(demultiplexer_2_out1), .Q(register_1_q), .clk(demultiplexer_1_out1), .clr(1'b0));  // open: en
  not not_1 (not_1_out, Ecrire_1_ou_Lire_0);
  Register register_2 (.D(demultiplexer_2_out0), .Q(register_2_q), .clk(demultiplexer_1_out0), .clr(1'b0));  // open: en
  Register register_3 (.D(demultiplexer_2_out2), .Q(register_3_q), .clk(demultiplexer_1_out2), .clr(1'b0));  // open: en
  Register register_4 (.D(demultiplexer_2_out3), .Q(register_4_q), .clk(demultiplexer_1_out3), .clr(1'b0));  // open: en
  Multiplexer #(.select(2), .width(8)) multiplexer_1 (
    .in0(register_2_q), .in1(register_1_q), .in2(register_3_q), .in3(register_4_q), .out(multiplexer_1_out),
    .sel(adresse), .en(not_1_out));
  // Probe on multiplexer_1_out
  assign out_5 = not_1_out ? multiplexer_1_out : 8'bz;  // Controlled_Buffer controlled_buffer_1
endmodule

module \Unité_de_Calcul  (
  input  [7:0] \entré_8_bits_A ,
  input  [7:0] \entré_8_bits_B ,
  input  [1:0] \Opérande ,
  input  Activation___1,
  output Retenue,
  output \_1___debordement_de_la_somme_alors_le_résultat_est_faux ,
  output [7:0] \Résultat_8_bits ,
  output out_8
);

  wire [7:0] adder_1_out, divider_1_out, multiplier_1_out, subtractor_1_out;

  // Probe on \entré_8_bits_A 
  // Probe on \entré_8_bits_B 
  Adder adder_1 (
    .a(\entré_8_bits_A ), .b(\entré_8_bits_B ), .out(adder_1_out),
    .cout(\_1___debordement_de_la_somme_alors_le_résultat_est_faux ));  // open: cin
  Subtractor subtractor_1 (
    .a(\entré_8_bits_A ), .b(\entré_8_bits_B ), .out(subtractor_1_out), .bin(1'b0), .bout(out_8));
  Multiplier multiplier_1 (.a(\entré_8_bits_A ), .b(\entré_8_bits_B ), .out(multiplier_1_out));  // open: cin, cout
  Divider divider_1 (.a(\entré_8_bits_A ), .b(\entré_8_bits_B ), .out(divider_1_out));  // open: upper, rem
  Multiplexer #(.select(2), .width(8)) multiplexer_1 (
    .in0(adder_1_out), .in1(subtractor_1_out), .in2(multiplier_1_out), .in3(divider_1_out),
    .out(\Résultat_8_bits ), .sel(\Opérande ), .en(Activation___1));
  // Probe on \Résultat_8_bits 

  assign Retenue = \_1___debordement_de_la_somme_alors_le_résultat_est_faux ;
endmodule

module Sequenceur (
  input  [14:0] INSTRUCTIONS,
  output \Si_1_Alors_debordement___mauvais_résultat ,
  output Retenue,
  output [7:0] \résultat 
);

  wire and_1_out, clock_1_out, clock_2_out, clock_3_out, clock_4_out, clock_5_out, clock_6_out,
       comparator_1_eq, comparator_2_lt, comparator_3_eq, comparator_4_eq, comparator_5_eq, not_1_out,
       not_2_out, not_3_out, not_4_out, not_5_out, part_1_out_3, part_2_out_3;
  wire [1:0] controlled_buffer_2_out, multiplexer_1_out;
  wire [2:0] controlled_buffer_1_out_2, controlled_buffer_5_out;
  wire [7:0] \banc_de_régistre_1_out_5 , controlled_buffer_3_out, controlled_buffer_4_out,
       controlled_buffer_6_out, controlled_buffer_8_out, controlled_buffer_9_out, controlled_buffer_10_out,
       controlled_buffer_11_out, controlled_buffer_12_out, controlled_buffer_13_out, demultiplexer_1_out0,
       demultiplexer_1_out1, register_1_q, register_2_q, register_4_q, \unité_de_calcul_1_résultat_8_bits ;
  wire [11:0] controlled_buffer_1_out;

  assign {controlled_buffer_1_out_2, controlled_buffer_1_out} = not_1_out ? INSTRUCTIONS : 15'bz;  // Controlled_Buffer controlled_buffer_1
  Comparator #(.width(15)) comparator_1 (.a(INSTRUCTIONS), .b({15{1'b0}}), .eq(comparator_1_eq));  // open: gt, lt
  not not_1 (not_1_out, comparator_1_eq);
  Comparator #(.width(4)) comparator_2 (
    .a({1'b0, controlled_buffer_1_out_2}), .b(4'b0100), .lt(comparator_2_lt));  // open: gt, eq
  Comparator #(.width(4)) comparator_3 (
    .a({1'b0, controlled_buffer_1_out_2}), .b(4'b0100), .eq(comparator_3_eq));  // open: gt, lt
  Comparator #(.width(4)) comparator_4 (
    .a({1'b0, controlled_buffer_1_out_2}), .b(4'b0101), .eq(comparator_4_eq));  // open: gt, lt
  Comparator #(.width(4)) comparator_5 (
    .a({1'b0, controlled_buffer_1_out_2}), .b(4'b0110), .eq(comparator_5_eq));  // open: gt, lt
  assign controlled_buffer_2_out = comparator_2_lt ? controlled_buffer_1_out[3:2] : 2'bz;  // Controlled_Buffer controlled_buffer_2
  assign controlled_buffer_3_out = comparator_3_eq ? controlled_buffer_1_out[11:4] : 8'bz;  // Controlled_Buffer controlled_buffer_3
  assign controlled_buffer_4_out = not_2_out ? controlled_buffer_3_out : 8'bz;  // Controlled_Buffer controlled_buffer_4
  assign controlled_buffer_5_out = comparator_2_lt ? controlled_buffer_1_out_2 : 3'bz;  // Controlled_Buffer controlled_buffer_5
  not not_2 (not_2_out, comparator_4_eq);
  not not_3 (not_3_out, comparator_5_eq);
  assign controlled_buffer_6_out = not_3_out ? controlled_buffer_4_out : 8'bz;  // Controlled_Buffer controlled_buffer_6
  not not_4 (not_4_out, comparator_2_lt);
  and and_1 (and_1_out, not_4_out, not_4_out, not_3_out, not_3_out);
  // Probe on controlled_buffer_1_out[1:0]
  Multiplexer #(.width(2)) multiplexer_1 (
    .in0(controlled_buffer_1_out[1:0]), .in1(controlled_buffer_2_out), .out(multiplexer_1_out),
    .sel(clock_1_out), .en(1'b1));
  Clock #(.highDuration(4), .lowDuration(4)) clock_1 (.out(clock_1_out));
  assign controlled_buffer_6_out = comparator_4_eq ? register_4_q : 8'bz;  // Controlled_Buffer controlled_buffer_7
  assign controlled_buffer_8_out = comparator_2_lt ? \banc_de_régistre_1_out_5  : 8'bz;  // Controlled_Buffer controlled_buffer_8
  \Banc_de_Régistre  \banc_de_régistre_1  (
    .\Entré (controlled_buffer_6_out), .Ecrire_1_ou_Lire_0(and_1_out), .adresse(multiplexer_1_out),
    .Activation(and_1_out), .out_5(\banc_de_régistre_1_out_5 ));
  Demultiplexer #(.width(8)) demultiplexer_1 (
    .out0(demultiplexer_1_out0), .out1(demultiplexer_1_out1), .in(controlled_buffer_8_out),
    .sel(clock_2_out), .en(1'b1));
  Clock #(.highDuration(2), .lowDuration(2)) clock_2 (.out(clock_2_out));
  not not_5 (not_5_out, clock_1_out);
  assign controlled_buffer_9_out = not_5_out ? demultiplexer_1_out0 : 8'bz;  // Controlled_Buffer controlled_buffer_9
  assign controlled_buffer_10_out = not_5_out ? demultiplexer_1_out1 : 8'bz;  // Controlled_Buffer controlled_buffer_10
  assign controlled_buffer_11_out = part_2_out_3 ? controlled_buffer_9_out : 8'bz;  // Controlled_Buffer controlled_buffer_11
  assign controlled_buffer_12_out = part_1_out_3 ? controlled_buffer_10_out : 8'bz;  // Controlled_Buffer controlled_buffer_12
  Register register_1 (.D(controlled_buffer_11_out), .en(1'b1), .Q(register_1_q), .clk(clock_3_out), .clr(1'b0));
  Clock clock_3 (.out(clock_3_out));
  Register register_2 (.D(controlled_buffer_12_out), .en(1'b1), .Q(register_2_q), .clk(clock_4_out), .clr(1'b0));
  Clock clock_4 (.out(clock_4_out));
  circuit part_1 (.in_1(controlled_buffer_10_out), .in_2({8{1'b0}}), .out_3(part_1_out_3));
  assign controlled_buffer_13_out = comparator_5_eq ? \banc_de_régistre_1_out_5  : 8'bz;  // Controlled_Buffer controlled_buffer_13
  circuit part_2 (.in_1(controlled_buffer_9_out), .in_2({8{1'b0}}), .out_3(part_2_out_3));
  Register register_3 (.D(controlled_buffer_13_out), .en(1'b1), .Q(\résultat ), .clk(clock_5_out), .clr(1'b0));
  Clock clock_5 (.out(clock_5_out));
  \Unité_de_Calcul  \unité_de_calcul_1  (
    .\entré_8_bits_A (register_1_q), .\entré_8_bits_B (register_2_q),
    .\Opérande (controlled_buffer_5_out[1:0]), .Activation___1(1'b1), .Retenue(Retenue),
    .\_1___debordement_de_la_somme_alors_le_résultat_est_faux (\Si_1_Alors_debordement___mauvais_résultat ),
    .\Résultat_8_bits (\unité_de_calcul_1_résultat_8_bits ));  // open: out_8
  Register register_4 (
    .D(\unité_de_calcul_1_résultat_8_bits ), .en(1'b1), .Q(register_4_q), .clk(clock_6_out), .clr(1'b0));
  Clock clock_6 (.out(clock_6_out));
  // Probe on \résultat 

  // Notes on the sheet:
  //   pour les 4 operations 
  //   On utilise 2REGISTRES qui nous aident dans les quatre opérations
endmodule

module circuit (
  input  [7:0] in_1,
  input  [7:0] in_2,
  output out_3
);

  wire comparator_1_eq;

  Comparator comparator_1 (.a(in_1), .b(in_2), .eq(comparator_1_eq));  // open: gt, lt
  not not_1 (out_3, comparator_1_eq);
endmodule
